# Fritzing sketch energy-consumption-monitor (saved by Fritzing 0.9.9b)

parts:
  Part1 = Arduino Uno (Rev3)
  GSM_SIM_GPSR_SMS_SIM900_SIM1 = SIM800L [package=THT]
  microSD1 = MicroSD Card Module
  ZS-042_RTC1 = ZS-042 RTC Module
  LCD2004-I2C1 = LCD2004-I2C
  Mod1 = zmpt101b
  Part2 = ACS712 Current Sensor 5A 20A 30A
  o1 = Module display OLED I2C 128x64 SSD1306 [package=THT]
  TP1 = TP4056 [chip_label=TP4056 package="DIP (Dual Inline) [THT]"]
  U2 = LIPO-110mAh [package=lipo-110]
  J1 = female pin header, 2 pins [form="♀ (female)"]
  J2 = female pin header, 2 pins [form="♀ (female)"]
  J3 = female pin header, 2 pins [form="♀ (female)"]
  J4 = female pin header, 2 pins [form="♀ (female)"]
  J5 = female pin header, 2 pins [form="♀ (female)"]
  J6 = female pin header, 2 pins [form="♀ (female)"]
  J7 = female pin header, 2 pins [form="♀ (female)"]
  J8 = female pin header, 2 pins [form="♀ (female)"]
  J9 = female pin header, 2 pins [form="♀ (female)"]
  J10 = female pin header, 2 pins [form="♀ (female)"]
  M1 = RioRand LM2596
  J11 = female pin header, 2 pins [form="♀ (female)"]
  J12 = female pin header, 2 pins [form="♀ (female)"]
  J13 = female pin header, 2 pins [form="♀ (female)"]
  J14 = female pin header, 2 pins [form="♀ (female)"]
  J15 = female pin header, 2 pins [form="♀ (female)"]
  J16 = female pin header, 2 pins [form="♀ (female)"]

nets:
  N1: Part1.A0, Mod1.OUT, J12.pin2
  N2: Part1.A1, Part2.2, Part2.OUT, J12.pin1
  N3: Part1.D10_PWM/SS, microSD1.CS
  N4: Part1.D11_PWM/MOSI, microSD1.MOSI
  N5: Part1.D12/MISO, microSD1.MISO
  N6: Part1.D13/SCK, microSD1.SCK
  N7: Part1.GND, GSM_SIM_GPSR_SMS_SIM900_SIM1.GND#5, J15.pin1, J16.pin1
  N8: Part1.A4/SDA, ZS-042_RTC1.SDA
  N9: Part1.A5/SCL, ZS-042_RTC1.SCL
  N10: Part1.D5_PWM, GSM_SIM_GPSR_SMS_SIM900_SIM1.SIM_TXD
  N11: Part1.D6_PWM, GSM_SIM_GPSR_SMS_SIM900_SIM1.SIM_RXD
  N12: Part1.5V, J15.pin2, J16.pin2
  N13: GSM_SIM_GPSR_SMS_SIM900_SIM1.5V, J8.pin2
  N14: GSM_SIM_GPSR_SMS_SIM900_SIM1.GND#1, J8.pin1
  N15: microSD1.GND, J1.pin2
  N16: microSD1.VCC, J1.pin1
  N17: ZS-042_RTC1.GND, J3.pin2
  N18: ZS-042_RTC1.VCC, J3.pin1
  N19: LCD2004-I2C1.GND, J2.pin1
  N20: LCD2004-I2C1.VCC, J2.pin2
  N21: LCD2004-I2C1.SDA, J4.pin1
  N22: LCD2004-I2C1.SCL, J4.pin2
  N23: Mod1.VCC, J7.pin2, J14.pin2
  N24: Mod1.GND, J7.pin1, J14.pin1
  N25: Part2.VCC, J11.pin1, J13.pin1
  N26: Part2.GND, J11.pin2, J13.pin2
  N27: o1.GND, J5.pin1
  N28: o1.VCC, J5.pin2
  N29: o1.SCL, J6.pin1
  N30: o1.SDA, J6.pin2
  N31: TP1.pin1, J9.pin1
  N32: TP1.pin2, J9.pin2
  N33: TP1.pin3, M1.Pin_1
  N34: TP1.pin4, U2.+
  N35: TP1.pin5, U2.-
  N36: TP1.pin6, M1.Pin_2
  N37: J10.pin1, M1.Pin_3
  N38: J10.pin2, M1.Pin_4

custom parts:
  LCD2004-I2C: A standard character display with 4x20 characters. Comes in many colors with LCM2004 IIC attached.
  zmpt101b: Single phase ac active output voltate transformer module.
  ACS712 Current Sensor 5A 20A 30A: Remix by Michael Kubina http://www.kubina.info Original by: https://forum.fritzing.org/t/current-sensor-5a-acs712/7694 https://forum.fritzing.org/u/ArtHome ArtHome12@gmail.com
  Module display OLED I2C 128x64 SSD1306: Ecran OLED I2C SSD163 de 128x64 avec connexion I2C
  TP4056: A DIP stand-in part for whatever IC you want. With 6 pins on a 300mil dual inline package (DIP) footprint.
